# Fritzing sketch Skecth (saved by Fritzing 0.9.3b)
breadboards: 2

parts:
  Part1 = Adafruit TCA9548A
  Part2 = Adafruit Feather HUZZAH ESP8266 [part_number="Adafruit #2821"]
  SDA6 = Header 1 [package=snap-female]
  Vibro = Header 1 [package=snap-female]
  SCL5 = Header 1 [package=snap-female]
  SDA5 = Header 1 [package=snap-female]
  SCL6 = Header 1 [package=snap-female]
  DATA1 = Header 1 [package=snap-female]
  GND = Header 1 [package=snap-female]
  VCC = Header 1 [package=snap-female]
  DATA2 = Header 1 [package=snap-female]
  GY-87 = GY-521 (MPU-6050) [form="♀ (female)" package=THT]
  GY-87_2 = GY-521 (MPU-6050) [form="♀ (female)" package=THT]
  VCC_2 = Header 1 [package=snap-female]
  GND_2 = Header 1 [package=snap-female]
  SCL = Header 1 [package=snap-female]
  VCC_3 = Header 1 [package=snap-female]
  SDA = Header 1 [package=snap-female]
  SCL_2 = Header 1 [package=snap-female]
  GND_3 = Header 1 [package=snap-female]
  SDA_2 = Header 1 [package=snap-female]
  Part3 = NeoPixel Stick [part_number=1426]
  Part4 = NeoPixel Stick [part_number=1426]
  GND_4 = Header 1 [package=snap-female]
  DATA = Header 1 [package=snap-female]
  VCC_4 = Header 1 [package=snap-female]
  GND_5 = Header 1 [package=snap-female]
  DATA_2 = Header 1 [package=snap-female]
  VCC_5 = Header 1 [package=snap-female]
  BAT1 = Battery Holders [package=lipo-1100mAh]
  Vibro_2 = Vibration Motor- ROB-08449 [package=vibe-motor-10mm]
  SCL7 = Header 1 [package=snap-female]
  SCL8 = Header 1 [package=snap-female]
  JP16 = Header 2 [package=jst-2-pth-kit]  # not connected

nets:
  N1: Part1.5SDA, SCL5.1
  N2: Part1.5SCL, SDA5.1
  N3: Part1.6SDA, SCL6.1
  N4: Part1.6SCL, SDA6.1
  VCC: Part1.VCC, Part2.3.3V
  GND: Part1.GND, Part2.GND
  N5: Part1.INPUTSDA, Part2.GPIO4/SDA
  N6: Part1.INPUTSCL, Part2.GPIO5/SCL
  N7: Part2.GPIO12/MISO, DATA2.1
  N8: Part2.GPIO13/MOSI, DATA1.1
  N9: Part2.GPIO15, Vibro.1
  N10: GND.1, BAT1.-
  N11: VCC.1, BAT1.+
  N12: GY-87.pin1, VCC_2.1
  N13: GY-87.pin2, GND_3.1
  N14: GY-87.pin3, SCL_2.1
  N15: GY-87.pin4, SDA.1
  N16: GY-87_2.pin1, VCC_3.1
  N17: GY-87_2.pin2, GND_2.1
  N18: GY-87_2.pin3, SCL.1
  N19: GY-87_2.pin4, SDA_2.1
  N20: Part3.GND, GND_4.1
  N21: Part3.DATAOUT, DATA.1
  N22: Part3.+5V, VCC_4.1
  N23: Part4.GND, GND_5.1
  N24: Part4.DATAOUT, DATA_2.1
  N25: Part4.+5V, VCC_5.1
  N26: Vibro_2.+, SCL8.1
  N27: Vibro_2.-, SCL7.1

custom parts:
  Adafruit TCA9548A: You just found the perfect I2C sensor, and you want to wire up two or three or more of them to your Arduino when you realize "Uh oh, this chip has a fixed I2C address, and from what I know about I2C, you cannot have two devices with the same address on the same SDA/SCL pins!" Are you out of luck? You would be, if you didn't have this ultra-cool TCA9548A 1-to-8 I2C multiplexer! Finally, a way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
  Adafruit Feather HUZZAH ESP8266: his is the Adafruit Feather HUZZAH ESP8266 - our take on an 'all-in-one' ESP8266 WiFi development board with built in USB and battery charging. Its an ESP8266 WiFi module with all the extras you need, ready to rock! We have other boards in the Feather family, check'em out here. At the Feather HUZZAH's heart is an ESP8266 WiFi microcontroller clocked at 80 MHz and at 3.3V logic. This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
  GY-521 (MPU-6050): Placa GY-521 basada en conjunto de acelerómetro+giroscopios MPU-6050
  NeoPixel Stick: Make your own little LED strip arrangement with this stick of NeoPixel LEDs. We crammed 8 of the tiny 5050 (5mm x 5mm) smart RGB LEDs onto a PCB with mounting holes and a chainable design. Use only one microcontroller pin to control as many as you can chain together! Each LED is addressable as the driver chip is inside the LED. Each one has ~18mA constant current drive so the color will be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
